// Logisim project COA PROJECT.circ as structural Verilog: 1 circuit, main circuit main
module main (
  input  in_1,
  input  in_2,
  input  in_3,
  input  in_4,
  input  in_5,
  input  in_6,
  input  in_7,
  input  in_8,
  input  SL,
  input  SR,
  input  SL_2,
  input  SR_2,
  input  in_13,
  input  in_14,
  input  in_15,
  input  in_16,
  input  in_17,
  input  in_18,
  input  in_19,
  input  in_20,
  input  in_21,
  input  in_22,
  input  in_23,
  input  in_24,
  input  [1:0] S1_S0,
  input  [1:0] S3_S2,
  output D3,
  output F0,
  output F1,
  output F2,
  output F3
);

  wire adder_1_out, adder_2_cout, adder_2_out, adder_3_cout, adder_3_out, adder_4_cout, adder_4_out,
       and_1_out, and_2_out, and_3_out, and_4_out, multiplexer_1_out, multiplexer_2_out, multiplexer_3_out,
       multiplexer_5_out, multiplexer_9_out, multiplexer_10_out, multiplexer_11_out, multiplexer_12_out,
       multiplexer_13_out, multiplexer_14_out, multiplexer_15_out, multiplexer_16_out, multiplexer_17_out,
       multiplexer_18_out, multiplexer_19_out, multiplexer_20_out, multiplexer_21_out, multiplexer_22_out,
       multiplexer_23_out, multiplexer_24_out, not_1_out, not_2_out, not_3_out, not_5_out, not_6_out,
       not_7_out, not_8_out, not_9_out, or_1_out, or_2_out, or_3_out, or_4_out, xor_1_out, xor_2_out,
       xor_3_out, xor_4_out;

  not not_1 (not_1_out, in_4);
  Multiplexer #(.select(2)) multiplexer_1 (
    .in0(in_4), .in1(not_1_out), .in2(not_2_out), .in3(in_13), .out(multiplexer_1_out), .sel(S1_S0),
    .en(in_20));
  Adder #(.width(1)) adder_1 (.a(in_8), .b(multiplexer_1_out), .out(adder_1_out), .cin(adder_2_cout), .cout(D3));
  not not_2 (not_2_out, in_3);
  Adder #(.width(1)) adder_2 (
    .a(in_7), .b(multiplexer_2_out), .out(adder_2_out), .cin(adder_3_cout), .cout(adder_2_cout));
  Multiplexer #(.select(2)) multiplexer_2 (
    .in0(in_3), .in1(not_2_out), .in2(not_2_out), .in3(in_13), .out(multiplexer_2_out), .sel(S1_S0),
    .en(in_21));
  not not_3 (not_3_out, in_2);
  Multiplexer #(.select(2)) multiplexer_3 (
    .in0(in_2), .in1(not_3_out), .in2(not_2_out), .in3(in_13), .out(multiplexer_3_out), .sel(S1_S0),
    .en(in_22));
  Adder #(.width(1)) adder_3 (
    .a(in_6), .b(multiplexer_3_out), .out(adder_3_out), .cin(adder_4_cout), .cout(adder_3_cout));
  Multiplexer #(.select(2)) multiplexer_4 (
    .in0(adder_1_out), .in1(multiplexer_15_out), .in2(multiplexer_17_out), .in3(multiplexer_21_out),
    .out(F3), .sel(S3_S2));  // open: en
  not not_4 (not_2_out, in_13);
  not not_5 (not_5_out, in_1);
  Multiplexer #(.select(2)) multiplexer_5 (
    .in0(in_1), .in1(not_5_out), .in2(not_2_out), .in3(in_13), .out(multiplexer_5_out), .sel(S1_S0),
    .en(in_23));
  Adder #(.width(1)) adder_4 (.a(in_5), .b(multiplexer_5_out), .out(adder_4_out), .cin(in_24), .cout(adder_4_cout));
  Multiplexer #(.select(2)) multiplexer_6 (
    .in0(adder_2_out), .in1(multiplexer_13_out), .in2(multiplexer_18_out), .in3(multiplexer_22_out),
    .out(F2), .sel(S3_S2));  // open: en
  Multiplexer #(.select(2)) multiplexer_7 (
    .in0(adder_3_out), .in1(multiplexer_11_out), .in2(multiplexer_19_out), .in3(multiplexer_23_out),
    .out(F1), .sel(S3_S2));  // open: en
  Multiplexer #(.select(2)) multiplexer_8 (
    .in0(adder_4_out), .in1(multiplexer_9_out), .in2(multiplexer_20_out), .in3(multiplexer_24_out), .out(F0),
    .sel(S3_S2));  // open: en
  and and_1 (and_1_out, in_5, in_1);
  or or_1 (or_1_out, in_5, in_1);
  Multiplexer #(.select(2)) multiplexer_9 (
    .in0(and_1_out), .in1(or_1_out), .in2(xor_1_out), .in3(not_6_out), .out(multiplexer_9_out), .sel(S1_S0));  // open: en
  xor xor_1 (xor_1_out, in_5, in_1);
  Multiplexer multiplexer_10 (.in0(in_5), .in1(in_1), .out(multiplexer_10_out), .sel(in_16));  // open: en
  not not_6 (not_6_out, multiplexer_10_out);
  and and_2 (and_2_out, in_6, in_2);
  or or_2 (or_2_out, in_6, in_2);
  Multiplexer #(.select(2)) multiplexer_11 (
    .in0(and_2_out), .in1(or_2_out), .in2(xor_2_out), .in3(not_7_out), .out(multiplexer_11_out), .sel(S1_S0));  // open: en
  xor xor_2 (xor_2_out, in_6, in_2);
  Multiplexer multiplexer_12 (.in0(in_6), .in1(in_2), .out(multiplexer_12_out), .sel(in_17));  // open: en
  not not_7 (not_7_out, multiplexer_12_out);
  and and_3 (and_3_out, in_7, in_3);
  or or_3 (or_3_out, in_7, in_3);
  Multiplexer #(.select(2)) multiplexer_13 (
    .in0(and_3_out), .in1(or_3_out), .in2(xor_3_out), .in3(not_8_out), .out(multiplexer_13_out), .sel(S1_S0));  // open: en
  xor xor_3 (xor_3_out, in_7, in_3);
  Multiplexer multiplexer_14 (.in0(in_7), .in1(in_3), .out(multiplexer_14_out), .sel(in_18));  // open: en
  not not_8 (not_8_out, multiplexer_14_out);
  and and_4 (and_4_out, in_8, in_4);
  or or_4 (or_4_out, in_8, in_4);
  xor xor_4 (xor_4_out, in_8, in_4);
  Multiplexer #(.select(2)) multiplexer_15 (
    .in0(and_4_out), .in1(or_4_out), .in2(xor_4_out), .in3(not_9_out), .out(multiplexer_15_out), .sel(S1_S0));  // open: en
  Multiplexer multiplexer_16 (.in0(in_8), .in1(in_4), .out(multiplexer_16_out), .sel(in_19));  // open: en
  not not_9 (not_9_out, multiplexer_16_out);
  Multiplexer multiplexer_17 (.in0(SL), .in1(in_8), .out(multiplexer_17_out), .sel(in_14));  // open: en
  Multiplexer multiplexer_18 (.in0(in_7), .in1(in_6), .out(multiplexer_18_out), .sel(in_14));  // open: en
  Multiplexer multiplexer_19 (.in0(in_8), .in1(in_5), .out(multiplexer_19_out), .sel(in_14));  // open: en
  Multiplexer multiplexer_20 (.in0(in_6), .in1(SR), .out(multiplexer_20_out), .sel(in_14));  // open: en
  Multiplexer multiplexer_21 (.in0(SL_2), .in1(in_8), .out(multiplexer_21_out), .sel(in_15));  // open: en
  Multiplexer multiplexer_22 (.in0(in_7), .in1(in_6), .out(multiplexer_22_out), .sel(in_15));  // open: en
  Multiplexer multiplexer_23 (.in0(in_8), .in1(in_5), .out(multiplexer_23_out), .sel(in_15));  // open: en
  Multiplexer multiplexer_24 (.in0(in_6), .in1(SR_2), .out(multiplexer_24_out), .sel(in_15));  // open: en

  // Notes on the sheet:
  //   ARITHMATIC UNIT
  //   D2
  //   A0   A1   A2   A3
  //   D1
  //   D0
  //   B0    B1    B2    B3 
  //   E0
  //   E1
  //   LOGIC UNIT
  //   E2
  //   E3
  //   RIGHT SHIFT
  //   LEFT SHIFT
endmodule
